# Fritzing sketch dakboard (saved by Fritzing 0.9.4)

parts:
  Raspberry_Pi_1 = Raspberry Pi 3 [part_number=RPI-3-V1.2]
  PIR_Motion_Sensor = PIR sensor
  Blue_(Running)_LED = LEDs [package=led10mm]
  part = Resistor [tolerance=±5% resistance=2k package=THT]  # not connected
  part_2 = Resistor [tolerance=±5% resistance=2k package=THT]
  Green_(Motion)_LED = LEDs [package=led10mm]
  part_3 = Resistor [tolerance=±5% resistance=220 package=THT]
  F1 = Fan - Ventilador [package=THT]
  Control_Button = Pushbutton [package="[SMD]"]

nets:
  N1: Raspberry_Pi_1.GPIO4, PIR_Motion_Sensor.SIG
  GND: Raspberry_Pi_1.GND, PIR_Motion_Sensor.GND, part_2.Pin_0, part_3.Pin_0, F1.GND, Control_Button.Pin_3, Control_Button.Pin_4
  3V3: Raspberry_Pi_1.3V3, F1.5V
  N2: Raspberry_Pi_1.GPIO16, Control_Button.Pin_2
  N3: Raspberry_Pi_1.GPIO25, Green_(Motion)_LED.A
  N4: Raspberry_Pi_1.GPIO24, Blue_(Running)_LED.C
  5V: Raspberry_Pi_1.5V, PIR_Motion_Sensor.VDD

custom parts:
  Fan - Ventilador: Ventilador de 2 pines, se encuentra comunmente en computadoras de escritorio
